# Fritzing sketch music_lamp (saved by Fritzing 0.9.3b)

parts:
  元件1 = Adafruit MAX9814 Electret Microphone Amplifier [part_number="Adafruit #1713"]
  U1 = WS2812 RGB LED strip
  R1 = Rotary Potentiometer (Small) [maximum_resistance=100kΩ package=THT]
  R2 = Rotary Potentiometer (Small) [maximum_resistance=100kΩ package=THT]
  元件2 = Arduino Nano (Rev3.0)
  S1 = Pushbutton [package="[THT]"]

nets:
  N1: 元件1.GAIN, 元件2.3V3
  N2: 元件1.OUTPUT, 元件2.A0
  N3: U1.DIN, 元件2.D2
  N4: R1.leg1, R2.leg1, 元件2.5V
  N5: R1.wiper, 元件2.A2
  N6: R1.leg2, R2.leg2, 元件2.GND
  N7: R2.wiper, 元件2.A1
  N8: 元件2.D3, S1.Pin_2

notes:
  * 物料清单
  * 1.主控：Arduino Nano
  * 2.电位器*2
  * 3.按钮*1
  * 4.ws2812灯带*1
  * 4.max9814麦克风*1
  * 接线方式
  * 1.电位器两端引脚不分正反，分别接到5v，gnd，中间引脚一个接A1一个接A2
  * 2.按钮一个引脚接D3，一个接GND
  * 3.ws2812 +接5v，-接GND，DIN接D2
  * 4.max9814：
  ** GND-GND
  ** VDD-5V
  ** Gain-3v3
  ** OUT-A0

custom parts:
  Adafruit MAX9814 Electret Microphone Amplifier: Add an ear to your project with this well-designed electret microphone amplifier with AGC. This fully assembled and tested board comes with a 20-20KHz electret microphone soldered on. For the amplification, we use the Maxim MAX9814, a specialty chip that is designed for amplifying electret microphones in situations where the loudness of the audio isn't predictable. This fancy microphone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
  WS2812 RGB LED strip: WS2812 strip
